# Fritzing sketch BrazoRobótico2 (saved by Fritzing 0.9.3b)
circuit board: 6.88566cm x 5.36311cm
breadboards: 2

parts:
  Componente1 = Arduino Uno (Rev3)
  S2 = Pushbutton [package="[THT]"]
  S1 = Pushbutton [package="[THT]"]
  R1 = Resistor [tolerance=±5% resistance=10k package=THT]
  R2 = Resistor [tolerance=±5% resistance=10k package=THT]
  P4 = Rotary Potentiometer (Small) [maximum_resistance=100kΩ package=THT]
  P3 = Rotary Potentiometer (Small) [maximum_resistance=100kΩ package=THT]
  P2 = Rotary Potentiometer (Small) [maximum_resistance=100kΩ package=THT]
  P1 = Rotary Potentiometer (Small) [maximum_resistance=100kΩ package=THT]
  C1 = Electrolytic Capacitor [capacitance=470µF voltage=16V package="100 mil [THT, electrolytic]"]
  J1 = Basic Servo
  J2 = Basic Servo
  J3 = Basic Servo
  J4 = Basic Servo
  VCC1 = Battery
  BT1 = Bluetooth HC-06u [package=THT]
  C2 = Electrolytic Capacitor [capacitance=100nF voltage=16V package="100 mil [THT, electrolytic]"]

nets:
  N1: Componente1.A0, P1.wiper
  N2: Componente1.A1, P2.wiper
  N3: Componente1.A2, P3.wiper
  N4: Componente1.A3, P4.wiper
  N5: Componente1.D8, J3.pulse
  N6: Componente1.D9_PWM, J2.pulse
  N7: Componente1.D10_PWM/SS, BT1.TXD
  N8: Componente1.D11_PWM/MOSI, BT1.RXD
  N9: Componente1.D12/MISO, J1.pulse
  GND: Componente1.GND, R1.Pin_1, R2.Pin_1, P4.leg1, P3.leg1, P2.leg1, P1.leg1, C1.-, J1.gnd, J2.gnd, J3.gnd, J4.gnd, VCC1.-, BT1.GND, C2.-
  N10: Componente1.D2, S1.Pin_1, S1.Pin_2, R1.Pin_0
  N11: Componente1.D3_PWM, S2.Pin_1, S2.Pin_2, R2.Pin_0
  N12: Componente1.D7, J4.pulse
  5V: Componente1.5V, S2.Pin_3, S2.Pin_4, S1.Pin_3, S1.Pin_4, P4.leg2, P3.leg2, P2.leg2, P1.leg2, BT1.VCC
  VCC: C1.+, J1.vcc, J2.vcc, J3.vcc, J4.vcc, VCC1.+, C2.+

notes:
  Shield robotic arm
  IES Vicente Aleixandre

custom parts:
  Bluetooth HC-06u: Bluetooth HC-06 - face up, pins down 16.5mm x 37.5mm PCB
